# Fritzing sketch robotic_arm (saved by Fritzing 0.9.3b)
circuit board: 8.46667cm x 5.64444cm
breadboards: 1

parts:
  Raspberry_Pi_1 = Raspberry Pi 3 [part_number=RPI-3-V1.2]
  J1 = Basic Servo
  J2 = Basic Servo
  J3 = Basic Servo
  J4 = Basic Servo
  J5 = Basic Servo
  M1 = Dagu DGServo 9g (Top view) [part_number=RS001B]
  Pololu_A1 = Pololu A4988 [package=SO16]
  M3 = Dagu DGServo 9g (Top view) [part_number=RS001B]
  VCC1 = 4 x AAA Battery Mount
  U1 = LIPO-2000mAh [package=lipo-2000]
  U2 = LIPO-2000mAh [package=lipo-2000]
  U3 = LIPO-2000mAh [package=lipo-2000]
  M2 = Stepper Motor - Bipolar
  C1 = Electrolytic Capacitor [capacitance=47µF voltage=16V package="100 mil [THT, electrolytic]"]
  U4 = LIPO-2000mAh [package=lipo-2000]

nets:
  N1: Raspberry_Pi_1.GPIO2, Pololu_A1.DIR
  N2: Raspberry_Pi_1.GIPO4, Pololu_A1.STEP
  GND: Raspberry_Pi_1.GND, J1.gnd, J2.gnd, J3.gnd, J4.gnd, J5.gnd, M1.gnd, Pololu_A1.GND#8, M3.gnd, VCC1.-
  N3: Raspberry_Pi_1.GIPO7, J1.pulse
  N4: Raspberry_Pi_1.GIPO8, J2.pulse
  N5: Raspberry_Pi_1.GIPO25, J3.pulse
  N6: Raspberry_Pi_1.GIPO24, J4.pulse
  N7: Raspberry_Pi_1.GIPO23, J5.pulse
  N8: Raspberry_Pi_1.GIPO18, M3.pulse
  N9: Raspberry_Pi_1.GIPO15, M1.pulse
  VCC: J1.vcc, J2.vcc, J3.vcc, J4.vcc, J5.vcc, M1.vcc, Pololu_A1.VDD, M3.vcc, VCC1.+
  N10: Pololu_A1.RESET, Pololu_A1.SLEEP
  N11: Pololu_A1.1B, M2.A
  N12: Pololu_A1.1A, M2.C
  N13: Pololu_A1.2A, M2.B
  N14: Pololu_A1.2B, M2.D
  N15: Pololu_A1.GND#14, C1.-, U4.-
  N16: Pololu_A1.VMOT, U1.+, C1.+
  N17: U1.-, U2.+
  N18: U2.-, U3.+
  N19: U3.-, U4.+
